# Fritzing sketch project one (saved by Fritzing 0.9.3b)
breadboards: 2

parts:
  LCD1 = LCD screen
  PSU1 = Adjustable Breadboard Power Supply
  R1 = Trimmer Potentiometer [maximum_resistance=10kΩ package=THT]
  Part1 = RFID-RC522-v2
  A1 = Raspberry Pi 5
  DS1 = DS18B20 1-Wire Temperature Sensor [part_number=DS18B20]
  R2 = Resistor [tolerance=±5% resistance=10k package=THT]
  R3 = Resistor [tolerance=±5% resistance=10k package=THT]
  M1 = Dagu DGServo 9g (Top view) [part_number=RS001B]

nets (from the schematic view):
  N1: LCD1.VSS, PSU1.Vin-, R1.leg2
  N2: LCD1.VDD, PSU1.Vin+, R1.leg1
  N3: LCD1.V0, R1.wiper
  N4: PSU1.Vout+, Part1.3.3V
  GND: PSU1.Vout-, Part1.RST, A1.GND, DS1.GND, M1.gnd
  N5: A1.GPIO4, DS1.DQ, R2.Pin_0, R3.Pin_0
  N6: A1.GPIO24, M1.pulse
  N7: DS1.VDD, R2.Pin_1, R3.Pin_1

custom parts:
  RFID-RC522-v2: A simple China made RFID-RC522 Reader; do check the pin labels, as this is a MFRC522 based clone.
  Raspberry Pi 5: The RPi5, a faster version of the awesome Raspberry Pi4B ARM Board with 40 pin gpio.
